# Fritzing sketch VibrationMotorBasic (saved by Fritzing 1.0.6)
breadboards: 1

parts:
  L293D_-_IC = L293D [package=THT]
  M1_(ERM_Vibration_Motor) = DC Motor [voltage_(max)=6V voltage_(min)=3V]

nets:
  GPIO 13: L293D_-_IC.Enable_1
  GPIO 12: L293D_-_IC.In_1
  N1: L293D_-_IC.Out_1_(_Controlled_by_Enable_1_), M1_(ERM_Vibration_Motor).pin_1
  GND: L293D_-_IC.0V
  N2: L293D_-_IC.Out_2_(_Controlled_by_Enable_1_), M1_(ERM_Vibration_Motor).pin_2
  GPIO 14: L293D_-_IC.In_2
  Vin (5V USB Power): L293D_-_IC.+Vmotor, L293D_-_IC.+V
